# Fritzing sketch attiny13a_soil_sensor (saved by Fritzing 0.9.1b)
breadboards: 1

parts:
  U1 = ATTINY13 [package=dip]
  U2 = ESP8266 WiFi Module [part_number=ESP8266]
  J1 = AVR ISP 6 Pin [package=2x3_lock]
  D1 = SOLAR-IXYS [package=solarbit-12x1]
  VCC1 = Battery
  D2 = Schottky Diode [part_number=1N5817 package="300 mil [THT]"]
  JP1 = Header 3 [package=molex-1x3_lock]
  Pololu11U3F = Pololu U1V11F3
  D3 = Schottky Diode [part_number=1N5817 package="300 mil [THT]"]
  R1 = Resistor [tolerance=±5% resistance=47k package=THT]
  R2 = Resistor [tolerance=±5% resistance=47k package=THT]
  R3 = Resistor [tolerance=±5% resistance=47k package=THT]
  S1 = Pushbutton [package="[THT]"]
  R4 = Resistor [tolerance=±5% resistance=47k package=THT]
  S2 = Pushbutton [package="[THT]"]
  D4 = Schottky Diode [part_number=1N5817 package="Melf DO-213 AB [SMD]"]
  R5 = Resistor [tolerance=±5% resistance=1M package=THT]
  S3 = Pushbutton [package="[THT]"]
  R6 = Resistor [tolerance=±5% resistance=47k package=THT]
  JP2 = Header 4 [package=molex-1x4_lock]
  R7 = Resistor [tolerance=±5% resistance=1M package=THT]
  R8 = Resistor [tolerance=±5% resistance=470k package=THT]

nets (from the schematic view):
  N1: U1.PB5(NRES), J1.5
  GND: U1.GND, U2.GND, J1.6, D1.A, VCC1.-, JP1.3, Pololu11U3F.GND, R2.Pin_1, S1.Pin_3, S1.Pin_4, S2.Pin_1, S2.Pin_2, R5.Pin_1, JP2.4, R8.Pin_1
  N2: U1.PB0(MOSI), J1.4, D3.anode
  N3: U1.PB1(MISO), U2.GPIO_16, J1.1
  N4: U1.PB2(SCK_ADC1), J1.3
  N5: U1.VCC, J1.2, VCC1.+, D2.cathode, Pololu11U3F.EN, R6.Pin_0
  N6: U2.RXD, JP2.3
  N7: U2.VCC, JP1.2, Pololu11U3F.OUT, R1.Pin_1, R3.Pin_0, R4.Pin_0, JP2.1
  N8: U2.GPIO_0, R4.Pin_1, S2.Pin_3, S2.Pin_4
  N9: U2.CH_PD, R1.Pin_0
  N10: U2.TXD, JP2.2
  N11: U2.GPIO_15, R2.Pin_0
  N12: U2.GPIO_5, D4.anode
  N13: U2.ADC_0, R7.Pin_0, R8.Pin_0
  N14: U2.REST, R3.Pin_1, S1.Pin_1, S1.Pin_2
  N15: D1.C, D2.anode
  N16: JP1.1, R7.Pin_1
  N17: Pololu11U3F.IN, D3.cathode, D4.cathode, R5.Pin_0, S3.Pin_4
  N18: S3.Pin_1, R6.Pin_1

custom parts:
  ESP8266 WiFi Module: Generic WiFi Module based on the ESP8266 with onboard PCB antenna and UART communications
  Pololu U1V11F3: Description: This is a 3.3V step up/down converter with enable pin.
